# Fritzing sketch schematic (saved by Fritzing 1.0.1rc)
perfboards: 1

parts:
  A1 = Arduino GIGA R1 WiFi
  A2 = Pololu m3s550 motor driver
  A3 = Pololu m3s550 motor driver
  GY1 = GY-521 (MPU-6050) 6pin [form="♀ (female)" package=THT]
  A4 = HC-SR04 Ultrasonic Distance Sensor
  U1 = QTR-9A Reflectance Sensor Array [package=THT]
  DC_Mot_Enc1 = DC Motor with two-phase hall-encoder [part_number=VT-E-G25A-06-177E]
  DC_Mot_Enc2 = DC Motor with two-phase hall-encoder [part_number=VT-E-G25A-06-177E]
  DC_Mot_Enc3 = DC Motor with two-phase hall-encoder [part_number=VT-E-G25A-06-177E]
  DC_Mot_Enc4 = DC Motor with two-phase hall-encoder [part_number=VT-E-G25A-06-177E]
  Part1 = RFID 2 WS1850S
  A5 = HC-SR04 Ultrasonic Distance Sensor
  A6 = HC-SR04 Ultrasonic Distance Sensor
  A7 = HC-SR04 Ultrasonic Distance Sensor
  A8 = HC-SR04 Ultrasonic Distance Sensor
  J1 = Basic Servo  # not connected
  VCC1 = Battery block 9V  # not connected
  S1 = Pushbutton [package="[THT]"]
  S2 = Pushbutton [package="[THT]"]
  S3 = Pushbutton [package="[THT]"]

nets:
  N1: A1.Pin_28, A1.Pin_29, A1.Pin_145, A1.Pin_146
  N2: A1.Pin_91, A6.TRIG
  N3: A1.Pin_92, A7.TRIG
  N4: A1.Pin_93, A5.TRIG
  N5: A1.Pin_94, A8.TRIG
  N6: A1.Pin_95, A4.TRIG
  N7: A1.Pin_96, A1.Pin_114, U1.9
  N8: A1.Pin_97, U1.7
  N9: A1.Pin_98, U1.5
  N10: A1.Pin_99, U1.3
  N11: A1.Pin_100, U1.1
  N12: A1.Pin_101, DC_Mot_Enc1.pin4
  N13: A1.Pin_102, DC_Mot_Enc3.pin4
  N14: A1.Pin_103, DC_Mot_Enc4.pin4
  N15: A1.Pin_104, DC_Mot_Enc2.pin4
  N16: A1.Pin_109, A6.ECHO
  N17: A1.Pin_110, A7.ECHO
  N18: A1.Pin_111, A5.ECHO
  N19: A1.Pin_112, A8.ECHO
  N20: A1.Pin_113, A4.ECHO
  N21: A1.Pin_115, U1.8
  N22: A1.Pin_116, U1.6
  N23: A1.Pin_117, U1.4
  N24: A1.Pin_118, U1.2
  N25: A1.Pin_119, DC_Mot_Enc1.pin5
  N26: A1.Pin_120, DC_Mot_Enc3.pin5
  N27: A1.Pin_121, DC_Mot_Enc4.pin5
  N28: A1.Pin_122, DC_Mot_Enc2.pin5
  N29: A1.Pin_124, Part1.SCL
  N30: A1.Pin_125, Part1.SDA
  N31: A1.Pin_143, A1.Pin_144
  N32: A1.Pin_147, A1.Pin_148, GY1.pin2
  N33: A1.Pin_149, GY1.pin1
  N34: A2.Pin_27, DC_Mot_Enc3.pin2
  N35: A2.Pin_28, DC_Mot_Enc3.pin1
  N36: A2.Pin_31, DC_Mot_Enc2.pin2
  N37: A2.Pin_32, DC_Mot_Enc2.pin1
  N38: A3.Pin_27, DC_Mot_Enc1.pin2
  N39: A3.Pin_28, DC_Mot_Enc1.pin1
  N40: A3.Pin_31, DC_Mot_Enc4.pin2
  N41: A3.Pin_32, DC_Mot_Enc4.pin1
  N42: S1.Pin_1, S1.Pin_2
  N43: S1.Pin_3, S1.Pin_4
  N44: S2.Pin_1, S2.Pin_2
  N45: S2.Pin_3, S2.Pin_4
  N46: S3.Pin_1, S3.Pin_2
  N47: S3.Pin_3, S3.Pin_4

custom parts:
  Arduino GIGA R1 WiFi: The Arduino GIGA R1 WiFi is designed for ambitious makers who want to step up their game.
  Pololu m3s550 motor driver: The Motoron M3S550 Triple Motor Controller Shield for Arduino makes it easy to control DC motors from an Arduino or Arduino-compatible board through an I²C interface.
  GY-521 (MPU-6050) 6pin: Placa GY-521 basada en conjunto de acelerómetro+giroscopios MPU-6050
  HC-SR04 Ultrasonic Distance Sensor: The HC-SR04 is an ultrasonic distance sensor. It is capable of providing measurement for ranges of 2cm to 400cm. The module operates at 5V.
  QTR-9A Reflectance Sensor Array: QTR-9A Reflectance Sensor Array (9 analog IR sensors with even/odd LED control).
  RFID 2 WS1850S: An I2C RFID reader module based on the WS1850S (MFRC522-compatible). 4-pin interface: SCL, SDA, 5V, GND.
